# Fritzing sketch blink_drum_relay (saved by Fritzing 0.9.3b)
breadboards: 1

parts:
  Part1 = Arduino Uno (Rev3)
  J1 = Screw terminal - 2 pins [package=THT]
  KY-2 = Keyes Relay [package=THT]
  L2 = Solenoid
  J2 = Infrared Proximity Sensor
  U1 = POT [package=pot_mammoth]

nets:
  N1: Part1.A0, J2.Vout
  N2: Part1.A1, U1.A
  N3: Part1.D8, KY-2.signal
  5V: Part1.5V, KY-2.power, J2.Vcc
  GND: Part1.GND, KY-2.ground, J2.GND, U1.S, U1.E
  N4: J1.pin1, KY-2.NO
  N5: KY-2.C, L2.pin1

notes:
  to mains adapter
  blink
  sensor
  sensitivity dial

custom parts:
  Keyes Relay: The Keyes 5V relay module is suitable for SCM development, home appliance control. It uses a 5V~12V TIL control signal which can control DC / AC signal.
